// Logisim project ALU.circ as structural Verilog: 1 circuit, main circuit ALU
module ALU (
  input  [31:0] A,
  input  [31:0] B,
  input  CarryIn,
  input  [4:0] Shift,
  input  [3:0] Codop,
  output [31:0] S,
  output [3:0] Flags
);

  wire and_4_out, and_5_out, and_6_out, and_7_out, and_10_out, and_11_out, and_12_out, and_13_out, Cadc,
       Casr, Ccmn, Ccmp, Clsl, Clsr, Cror, Csbc, not_1_out, not_3_out, not_4_out, not_5_out, not_7_out,
       not_8_out, not_9_out, Ntst, subtractor_3_bout, subtractor_6_bout, Vadc, Vcmn, Vcmp, Vrsb, Vsbc,
       xor_2_out, xor_3_out, xor_4_out, xor_5_out, Zcmn, Zcmp, ZS, Ztst;
  wire [4:0] and_1_out, and_2_out, and_8_out, subtractor_1_out, subtractor_2_out, subtractor_4_out;
  wire [30:0] lsrROR, tst;
  wire [31:0] adc, asr, bic, cmn, cmp, eor, et, lsl, lsr, mul, mvn, orr, rsb, sbc, shifter_1_out,
       shifter_2_out, shifter_7_out;

  Subtractor #(.width(5)) subtractor_1 (.a(Shift), .b(5'b00001), .out(subtractor_1_out));  // open: bin, bout
  Subtractor #(.width(5)) subtractor_2 (.a(Shift), .b(5'b00001), .out(subtractor_2_out));  // open: bin, bout
  Shifter #(.width(32)) shifter_1 (.in(B), .\dist (subtractor_1_out), .out(shifter_1_out));
  assign and_1_out = Shift & {5{1'b0}};  // AND_Gate and_1, 5 bits wide
  Shifter #(.shift("ar"), .width(32)) shifter_2 (.in(B), .\dist (subtractor_2_out), .out(shifter_2_out));
  assign and_2_out = Shift & {5{1'b0}};  // AND_Gate and_2, 5 bits wide
  assign et = A & B;  // AND_Gate and_3, 32 bits wide
  assign eor = A ^ B;  // XOR_Gate xor_1, 32 bits wide
  Shifter #(.width(32)) shifter_3 (.in(B), .\dist (Shift), .out(lsl));
  Shifter #(.shift("lr"), .width(32)) shifter_4 (.in(B), .\dist (Shift), .out(lsr));
  Multiplexer multiplexer_1 (.in0(shifter_1_out[31]), .in1(1'b0), .out(Clsl), .sel(and_1_out[0]));
  Multiplexer multiplexer_2 (.in0(shifter_2_out[0]), .in1(1'b0), .out(Casr), .sel(and_2_out[0]));
  Multiplexer #(.select(4)) multiplexer_3 (
    .in0(S[31]), .in1(S[31]), .in2(S[31]), .in3(S[31]), .in4(S[31]), .in5(S[31]), .in6(S[31]), .in7(S[31]),
    .in8(Ntst), .in9(S[31]), .in10(cmp[31]), .in11(cmn[31]), .in12(S[31]), .in13(S[31]), .in14(S[31]),
    .in15(S[31]), .out(Flags[3]), .sel(Codop));
  Multiplexer #(.select(4)) multiplexer_4 (
    .in0(1'b0), .in1(1'b0), .in2(Clsl), .in3(Clsr), .in4(Casr), .in5(Cadc), .in6(Csbc), .in7(Cror),
    .in8(1'b0), .in9(1'b0), .in10(Ccmp), .in11(Ccmn), .in12(1'b0), .in13(1'b0), .in14(1'b0), .in15(1'b0),
    .out(Flags[1]), .sel(Codop));
  not not_1 (not_1_out, CarryIn);
  Subtractor #(.width(32)) subtractor_3 (.a(B), .b(A), .out(sbc), .bin(not_1_out), .bout(subtractor_3_bout));
  not not_2 (Csbc, subtractor_3_bout);
  not not_3 (not_3_out, adc[31]);
  not not_4 (not_4_out, A[31]);
  not not_5 (not_5_out, B[31]);
  Shifter #(.shift("ar"), .width(32)) shifter_5 (.in(B), .\dist (Shift), .out(asr));
  Adder #(.width(32)) adder_1 (.a(A), .b(B), .out(adc), .cin(CarryIn), .cout(Cadc));
  Shifter #(.shift("rr"), .width(32)) shifter_6 (.in(B), .\dist (Shift), .out({Cror, lsrROR}));
  Subtractor #(.width(5)) subtractor_4 (.a(Shift), .b(5'b00001), .out(subtractor_4_out));  // open: bin, bout
  and and_4 (and_4_out, A[31], B[31]);
  and and_5 (and_5_out, and_4_out, not_3_out);
  and and_6 (and_6_out, not_4_out, not_5_out);
  and and_7 (and_7_out, and_6_out, adc[31]);
  Shifter #(.shift("lr"), .width(32)) shifter_7 (.in(B), .\dist (subtractor_4_out), .out(shifter_7_out));
  assign and_8_out = Shift & {5{1'b0}};  // AND_Gate and_8, 5 bits wide
  or or_1 (Vadc, and_5_out, and_7_out);
  Multiplexer #(.select(4), .width(32)) multiplexer_5 (
    .in0(et), .in1(eor), .in2(lsl), .in3(lsr), .in4(asr), .in5(adc), .in6(sbc), .in7({Cror, lsrROR}),
    .in8(B), .in9(rsb), .in10(B), .in11(B), .in12(orr), .in13(mul), .in14(bic), .in15(mvn), .out(S),
    .sel(Codop));
  Multiplexer #(.select(4)) multiplexer_6 (
    .in0(1'b0), .in1(1'b0), .in2(1'b0), .in3(1'b0), .in4(1'b0), .in5(Vadc), .in6(Vsbc), .in7(1'b0),
    .in8(1'b0), .in9(Vrsb), .in10(Vcmp), .in11(Vcmn), .in12(1'b0), .in13(1'b0), .in14(1'b0), .in15(1'b0),
    .out(Flags[0]), .sel(Codop));
  Multiplexer multiplexer_7 (.in0(shifter_7_out[0]), .in1(1'b0), .out(Clsr), .sel(and_8_out[0]));
  Multiplexer #(.select(4)) multiplexer_8 (
    .in0(ZS), .in1(ZS), .in2(ZS), .in3(ZS), .in4(ZS), .in5(ZS), .in6(ZS), .in7(ZS), .in8(Ztst), .in9(ZS),
    .in10(Zcmp), .in11(Zcmn), .in12(ZS), .in13(ZS), .in14(ZS), .in15(ZS), .out(Flags[2]), .sel(Codop));
  assign {Ntst, tst} = A & B;  // AND_Gate and_9, 32 bits wide
  Subtractor #(.width(32)) subtractor_5 (.a({32{1'b0}}), .b(A), .out(rsb), .bin(CarryIn));  // open: bout
  Subtractor #(.width(32)) subtractor_6 (.a(B), .b(A), .out(cmp), .bout(subtractor_6_bout));  // open: bin
  not not_6 (Ccmp, subtractor_6_bout);
  and and_10 (and_10_out, A[31], B[31]);
  not not_7 (not_7_out, cmn[31]);
  not not_8 (not_8_out, A[31]);
  not not_9 (not_9_out, B[31]);
  Adder #(.width(32)) adder_2 (.a(A), .b(B), .out(cmn), .cout(Ccmn));  // open: cin
  and and_11 (and_11_out, and_10_out, not_7_out);
  and and_12 (and_12_out, not_8_out, not_9_out);
  Comparator #(.width(32)) comparator_1 (.a(32'h80000000), .b(A), .eq(Vrsb));  // open: gt, lt
  and and_13 (and_13_out, and_12_out, cmn[31]);
  or or_2 (Vcmn, and_11_out, and_13_out);
  Comparator #(.width(32)) comparator_2 (.a(S), .b({32{1'b0}}), .eq(ZS));  // open: gt, lt
  Comparator #(.width(32)) comparator_3 (.a({Ntst, tst}), .b({32{1'b0}}), .eq(Ztst));  // open: gt, lt
  Comparator #(.width(32)) comparator_4 (.a(cmp), .b({32{1'b0}}), .eq(Zcmp));  // open: gt, lt
  Comparator #(.width(32)) comparator_5 (.a(cmn), .b({32{1'b0}}), .eq(Zcmn));  // open: gt, lt
  assign orr = A | B;  // OR_Gate or_3, 32 bits wide
  Multiplier #(.width(32)) multiplier_1 (.a(A), .b(B), .out(mul));  // open: cin, cout
  assign bic = B & mvn;  // AND_Gate and_14, 32 bits wide
  assign mvn = ~A;  // NOT_Gate not_10, 32 bits wide
  xor xor_2 (xor_2_out, B[31], sbc[31]);
  xor xor_3 (xor_3_out, A[31], B[31]);
  xor xor_4 (xor_4_out, A[31], B[31]);
  xor xor_5 (xor_5_out, B[31], cmp[31]);
  and and_15 (Vsbc, xor_3_out, xor_2_out);
  and and_16 (Vcmp, xor_4_out, xor_5_out);

  // Other names for the same wires on the sheet: ALU_Opcode[3:0] = Codop; CI = CarryIn; Ncmn = cmn[31];
  //   Ncmp = cmp[31]; V = Flags[0]; C = Flags[1]; Z = Flags[2]; N = Flags[3]; lsrROR[31] = Cror; NS = S[31];
  //   Shift_ALU[4:0] = Shift; tst[31] = Ntst

  // Notes on the sheet:
  //   Opérande A
  //   Opérande B
  //   Retenue entrante
  //   Nombre de décalages
  //   Sélecteur
  //   Résultat
  //   Drapeaux N,Z,C,V
  //   Note: for ROR, C = N
  //   ---------------- Ports : ---------------- 
  //   Note 2: assume that shift > 0 for LSL and LSR
  //   Calcul du flag C pour LSL
  //   Calcul du flag C pour LSR
  //   Bitwise AND
  //   Exclusive OR
  //   Logical Shift Left
  //   Logical Shift Right
  //   flag C (carry out)
  //   Flag N(négatif)
  //   Arithmetic Shift Right
  //   Add With Carry
  //   Substract With Carry
  //   Rotate Right
  //   Calcul du flag V pour ADC
  //   Calcul du flag C pour LSR
  //   ------------------------------------------------------------       Calculs des flags VC :       ------------------------------------------------------------
  //   ------------------------------------------------------------       Les 16 opérations possibles :       ------------------------------------------------------------
  //   Overflow (V)
  //   Set Flags on bitwise AND
  //   Flag Z(zéro)
  //   Set Flags on bitwise AND
  //   Compare Registers
  //   Compare Negative
  //   Calcul du flag V pour CMN
  //   B - A
  //   Calcul du flag C pour ROR
  //   Calcul du flag V pour RSB
  //   Calculs flags N(négatif)
  //   Calculs flags Z (zéro)
  //   Logical OR
  //   Multiply Two Registers
  //   Bit Clear
  //   Bitwise NOT
  //   Calcul du flag V pour SBC
  //   Calcul du flag V pour CMP
endmodule
