// Logisim project Ctl_Conditional.circ as structural Verilog: 1 circuit, main circuit Conditional
module Conditional (
  input  Z,
  input  [15:0] Instruction,
  input  C,
  input  N,
  input  V,
  input  Enable,
  output Verified,
  output [10:0] Offset
);

  wire and_1_out, and_2_out, comparator_1_eq, comparator_2_eq, multiplexer_2_out, not_1_out, not_2_out,
       not_3_out, not_4_out, not_5_out, not_6_out, not_7_out, or_1_out, or_2_out, xor_1_out, xor_2_out;
  wire [10:0] bit_extender_1_out;

  Comparator #(.width(1)) comparator_1 (.a(N), .b(V), .eq(comparator_1_eq));  // open: gt, lt
  and and_1 (and_1_out, C, not_1_out);
  not not_1 (not_1_out, Z);
  not not_2 (not_2_out, C);
  not not_3 (not_3_out, V);
  or or_1 (or_1_out, not_2_out, Z);
  xor xor_1 (xor_1_out, N, V);
  and and_2 (and_2_out, comparator_2_eq, not_4_out);
  not not_4 (not_4_out, Z);
  Comparator #(.width(1)) comparator_2 (.a(N), .b(V), .eq(comparator_2_eq));  // open: gt, lt
  not not_5 (not_5_out, N);
  or or_2 (or_2_out, Z, xor_2_out);
  xor xor_2 (xor_2_out, N, V);
  assign bit_extender_1_out = {{3{1'b0}}, Instruction[7:0]};  // Bit_Extender bit_extender_1
  not not_6 (not_6_out, Z);
  not not_7 (not_7_out, C);
  Multiplexer #(.width(11)) multiplexer_1 (
    .in0(bit_extender_1_out), .in1(Instruction[10:0]), .out(Offset), .sel(Instruction[13]));
  Multiplexer #(.select(4)) multiplexer_2 (
    .in0(Z), .in1(not_6_out), .in2(C), .in3(not_7_out), .in4(N), .in5(not_5_out), .in6(V), .in7(not_3_out),
    .in8(and_1_out), .in9(or_1_out), .in10(comparator_1_eq), .in11(xor_1_out), .in12(and_2_out),
    .in13(or_2_out), .in14(1'b1), .in15(1'b0), .out(multiplexer_2_out), .sel(Instruction[11:8]));
  and and_3 (Verified, multiplexer_2_out, Enable);

  // Other names for the same wires on the sheet: I[15:0] = Instruction; cond[3:0] = Instruction[11:8];
  //   signature[3:0] = Instruction[15:12]

  // Notes on the sheet:
  //   B imm11 = Instruction[15:11] == 11100
endmodule
