// Logisim project Ctl_Data_Processing.circ as structural Verilog: 2 circuits, main circuit Data_Processing
module Data_Processing (
  input  Enable,
  input  [15:0] Instruction,
  output [2:0] Rd,
  output [2:0] Rn,
  output [2:0] Rm,
  output [3:0] ALU_Opcode,
  output [3:0] Flags_Update_Mask
);

  wire [2:0] code02, code35;
  wire [3:0] flag_decoder_1_mask;
  wire [15:10] multiplexer_1_out;

  Multiplexer #(.width(16)) multiplexer_1 (
    .in0({16{1'b0}}), .in1(Instruction), .out({multiplexer_1_out, ALU_Opcode, code35, code02}), .sel(Enable));
  Flag_Decoder flag_decoder_1 (.entry(ALU_Opcode), .mask(flag_decoder_1_mask));
  Multiplexer #(.width(4)) multiplexer_2 (
    .in0(4'b0000), .in1(flag_decoder_1_mask), .out(Flags_Update_Mask), .sel(Enable));
  Multiplexer #(.select(4), .width(3)) multiplexer_3 (
    .in0(code02), .in1(code02), .in2(code02), .in3(code02), .in4(code02), .in5(code02), .in6(code02),
    .in7(code02), .in8(3'b000), .in9(code02), .in10(3'b000), .in11(3'b000), .in12(code02), .in13(code02),
    .in14(code02), .in15(code02), .out(Rd), .sel(ALU_Opcode));
  Multiplexer #(.select(4), .width(3)) multiplexer_4 (
    .in0(code02), .in1(code02), .in2(code02), .in3(code02), .in4(code02), .in5(code02), .in6(code02),
    .in7(code02), .in8(code02), .in9(code35), .in10(code02), .in11(code02), .in12(code02), .in13(code35),
    .in14(code02), .in15(3'b000), .out(Rn), .sel(ALU_Opcode));
  Multiplexer #(.select(4), .width(3)) multiplexer_5 (
    .in0(code35), .in1(code35), .in2(code35), .in3(code35), .in4(code35), .in5(code35), .in6(code35),
    .in7(code35), .in8(code35), .in9(3'b000), .in10(code35), .in11(code35), .in12(code35), .in13(code02),
    .in14(code35), .in15(code35), .out(Rm), .sel(ALU_Opcode));

  // Other names for the same wires on the sheet: opcode[3:0] = ALU_Opcode; rdout[2:0] = Rd; rmout[2:0] = Rm;
  //   rnout[2:0] = Rn

  // Notes on the sheet:
  //   Note 2: RSB instruction has Rn as 1st operand.
  //   MUL instruction has Rn as 1st operand and Rdm as 2nd operand
  //   For simplification purposes, Rm is used for 1st operand both here and in the ALU.
  //   Note: instructions that does not save the result will still have the second operand as the destination register, the ALU will copy the second register to the destination register
  //   Pull output low on Enable = 0
  //   Rd Ouput
  //   Rn Ouput
  //   Rm Ouput
endmodule

module Flag_Decoder (
  input  [3:0] entry,
  output [3:0] mask
);

  wire and_1_out, and_2_out, and_3_out, and_4_out, not_1_out, not_2_out, not_3_out, not_4_out;

  not not_1 (not_1_out, entry[3]);
  not not_2 (not_2_out, entry[2]);
  not not_3 (not_3_out, entry[1]);
  not not_4 (not_4_out, entry[0]);
  or or_1 (mask[1], not_1_out, not_2_out, not_4_out, entry[1]);
  and and_1 (and_1_out, not_1_out, entry[2], not_3_out, entry[0]);
  and and_2 (and_2_out, not_1_out, entry[2], entry[1], not_4_out);
  and and_3 (and_3_out, entry[3], not_2_out, entry[0]);
  and and_4 (and_4_out, entry[3], not_2_out, entry[1]);
  or or_2 (mask[0], and_1_out, and_2_out, and_3_out, and_4_out);

  assign mask[3:2] = 2'b11;
endmodule
