// Logisim project Ctl_Load_Store.circ as structural Verilog: 1 circuit, main circuit Load_Store
module Load_Store (
  input  [15:0] Instruction,
  input  Clk,
  input  Reset,
  input  [31:0] Stack_Pointer,
  input  Enable,
  output Store,
  output [2:0] Rmd,
  output Load,
  output [31:0] RAM_Addr,
  output PC_Hold
);

  wire d_ff_1_q, d_ff_2_q, Load_pre, PC_Hold_Calc, PcHold_pre, Store_Calc;
  wire [31:0] bit_extender_1_out, RAM_Addr_t;

  and and_1 (PC_Hold_Calc, Enable, Instruction[11]);
  D_Flip_Flop d_ff_1 (.D(Instruction[11]), .clk(Clk), .Q(d_ff_1_q), .reset(Reset));  // open: Qn, preset
  D_Flip_Flop d_ff_2 (.D(PC_Hold_Calc), .clk(Clk), .Q(d_ff_2_q), .reset(Reset));  // open: Qn, preset
  and and_2 (Store, Enable, Store_Calc);
  and and_3 (Load, Enable, Load_pre);
  and and_4 (PC_Hold, Enable, PcHold_pre);
  and and_5 (Load_pre, Enable, d_ff_1_q);
  and and_6 (PcHold_pre, Enable, d_ff_2_q);
  assign bit_extender_1_out = {{24{Instruction[7]}}, Instruction[7:0]};  // Bit_Extender bit_extender_1
  Multiplexer #(.width(3)) multiplexer_1 (.in0(3'b000), .in1(Instruction[10:8]), .out(Rmd), .sel(Enable));
  Multiplexer #(.width(32)) multiplexer_2 (.in0({32{1'b0}}), .in1(RAM_Addr_t), .out(RAM_Addr), .sel(Enable));
  not not_1 (Store_Calc, Instruction[11]);
  Adder #(.width(32)) adder_1 (.a(bit_extender_1_out), .b(Stack_Pointer), .out(RAM_Addr_t));  // open: cin, cout

  // Other names for the same wires on the sheet: Clock = Clk; imm8[7:0] = Instruction[7:0];
  //   Instruc[15:0] = Instruction; RegistreRt[2:0] = Instruction[10:8]; Load_Calc = Instruction[11];
  //   StoreOrLoad = Instruction[11]; SP[31:0] = Stack_Pointer

  // Notes on the sheet:
  //   Entrées
  //   Traduction instruction :
  //   Delay load and hold PC for 1 cycle for the RAM to send out requested data 
  //   Sorties
  //   Calcul RAM_Addr
  //   Identification de l'opération à faire :
endmodule
