// Logisim project Ctl_Shift_Add_Sub_Mov.circ as structural Verilog: 6 circuits, main circuit Shift_Add_Sub_Mov
module Shift_Add_Sub_Mov (
  input  Enable,
  input  [15:0] Instruction,
  output Carry,
  output Imm32_Enable,
  output [2:0] Rm,
  output [2:0] Rn,
  output [2:0] Rd,
  output [4:0] Imm5,
  output [31:0] Imm32,
  output [3:0] Flags_Update_Mask,
  output [3:0] ALU_Opcode
);

  wire [0:0] multiplexer_1_out_4;
  wire [2:0] multiplexer_1_out, multiplexer_1_out_2, multiplexer_1_out_3, multiplexer_1_out_5,
       multiplexer_3_out;
  wire [3:0] flag_decoder_1_flags, opcode_calculator_1_opcode;
  wire [3:3] multiplexer_1_out_6;
  wire [7:0] multiplexer_4_out;
  wire [15:14] multiplexer_1_out_7;
  wire [31:0] bit_extender_1_out, bit_extender_2_out, bit_extender_3_out, negator_1_out;

  Multiplexer #(.width(16)) multiplexer_1 (
    .in0({16{1'b0}}), .in1(Instruction),
    .out({multiplexer_1_out_7, multiplexer_1_out_6[3], multiplexer_1_out_5, multiplexer_1_out_4[0], multiplexer_1_out_3, multiplexer_1_out_2, multiplexer_1_out}),
    .sel(Enable));
  Multiplexer #(.select(3), .width(3)) multiplexer_2 (
    .in0(multiplexer_1_out_2), .in1(multiplexer_1_out_2), .in2(multiplexer_1_out_2),
    .in3(multiplexer_1_out_2), .in4(3'b000), .in5(3'b000),
    .in6({multiplexer_1_out_5[0], multiplexer_1_out_4[0], multiplexer_1_out_3[2]}),
    .in7({multiplexer_1_out_5[0], multiplexer_1_out_4[0], multiplexer_1_out_3[2]}), .out(Rn),
    .sel({multiplexer_1_out_6[3], multiplexer_1_out_5[2:1]}));
  Multiplexer #(.select(2), .width(3)) multiplexer_3 (
    .in0(3'b000), .in1(multiplexer_1_out_3), .in2(3'b000), .in3(3'b000), .out(multiplexer_3_out),
    .sel({multiplexer_1_out_6[3], multiplexer_1_out_5[0]}));
  Multiplexer #(.width(8)) multiplexer_4 (
    .in0({8{1'b0}}), .in1({multiplexer_1_out_3[1:0], multiplexer_1_out_2, multiplexer_1_out}),
    .out(multiplexer_4_out), .sel(multiplexer_1_out_6[3]));
  Carry_Enabler carry_enabler_1 (
    .OPCODE({multiplexer_1_out_6[3], multiplexer_1_out_5, multiplexer_1_out_4[0]}), .Enable(Carry));
  Imm32_Enabler imm32_enabler_1 (.Bit13(multiplexer_1_out_6[3]), .Bit1210(multiplexer_1_out_5), .Enable(Imm32_Enable));
  Rm_Pass rm_pass_1 (.Entry({multiplexer_1_out_6[3], multiplexer_1_out_5}), .Rm(multiplexer_1_out_3), .Output(Rm));
  Multiplexer #(.width(3)) multiplexer_5 (
    .in0(multiplexer_1_out), .in1({multiplexer_1_out_5[0], multiplexer_1_out_4[0], multiplexer_1_out_3[2]}),
    .out(Rd), .sel(multiplexer_1_out_6[3]));
  Multiplexer #(.select(3), .width(5)) multiplexer_6 (
    .in0({multiplexer_1_out_5[0], multiplexer_1_out_4[0], multiplexer_1_out_3}),
    .in1({multiplexer_1_out_5[0], multiplexer_1_out_4[0], multiplexer_1_out_3}),
    .in2({multiplexer_1_out_5[0], multiplexer_1_out_4[0], multiplexer_1_out_3}), .in3({5{1'b0}}),
    .in4({5{1'b0}}), .in5({5{1'b0}}), .in6({5{1'b0}}), .in7({5{1'b0}}), .out(Imm5),
    .sel({multiplexer_1_out_6[3], multiplexer_1_out_5[2:1]}));
  assign bit_extender_1_out = {{29{1'b0}}, multiplexer_3_out};  // Bit_Extender bit_extender_1
  assign bit_extender_2_out = {{24{1'b0}}, multiplexer_4_out};  // Bit_Extender bit_extender_2
  Flag_Decoder flag_decoder_1 (
    .OPCODE({multiplexer_1_out_6[3], multiplexer_1_out_5, multiplexer_1_out_4[0]}),
    .FLAGS(flag_decoder_1_flags));
  Opcode_Calculator opcode_calculator_1 (
    .entry({multiplexer_1_out_6[3], multiplexer_1_out_5, multiplexer_1_out_4[0]}),
    .opcode(opcode_calculator_1_opcode));
  Negator #(.width(32)) negator_1 (.in(bit_extender_2_out), .out(negator_1_out));
  assign bit_extender_3_out = {{24{1'b0}}, multiplexer_4_out};  // Bit_Extender bit_extender_3
  Multiplexer #(.width(4)) multiplexer_7 (
    .in0(4'b0000), .in1(flag_decoder_1_flags), .out(Flags_Update_Mask), .sel(Enable));
  Multiplexer #(.width(4)) multiplexer_8 (
    .in0(4'b0000), .in1(opcode_calculator_1_opcode), .out(ALU_Opcode), .sel(Enable));
  Multiplexer #(.select(3), .width(32)) multiplexer_9 (
    .in0({32{1'b0}}), .in1({32{1'b0}}), .in2({32{1'b0}}), .in3(bit_extender_1_out), .in4(negator_1_out),
    .in5(bit_extender_3_out), .in6(bit_extender_3_out), .in7(bit_extender_3_out), .out(Imm32),
    .sel({multiplexer_1_out_6[3], multiplexer_1_out_5[2:1]}));

  // Notes on the sheet:
  //   Note 3: Imm32_Enable forces the use of the immediate for Rm register
  //   Note: ALU uses Rn register for shifts. Use Rn instead of Rm for shifts (immediate) here too
  //   Note 2: MOV uses RSB ALU opcode with Imm8 reversed so that it is copied to output register
  //   Pull output low on Enable = 0
  //   only ADD and SUB use Rm
  //   Enable carry for SUB since it is reversed in ALU
  //   ALU will use Imm32 instead of Rm
endmodule

module Imm32_Enabler (
  input  Bit13,
  input  [2:0] Bit1210,
  output Enable
);

  wire and_1_out;

  and and_1 (and_1_out, Bit1210[2], Bit1210[1], Bit1210[0]);
  or or_1 (Enable, and_1_out, Bit13);
endmodule

module Rm_Pass (
  input  [3:0] Entry,
  input  [2:0] Rm,
  output [2:0] Output
);

  wire not_1_out, not_2_out;

  not not_1 (not_1_out, Entry[3]);
  not not_2 (not_2_out, Entry[0]);
  and and_1 (Output[2], not_1_out, Entry[2], Entry[1], not_2_out, Rm[2]);
  and and_2 (Output[1], not_1_out, Entry[2], Entry[1], not_2_out, Rm[1]);
  and and_3 (Output[0], not_1_out, Entry[2], Entry[1], not_2_out, Rm[0]);
endmodule

module Carry_Enabler (
  input  [4:0] OPCODE,
  output Enable
);

  wire and_1_out, and_2_out;

  and and_1 (and_1_out, OPCODE[4], OPCODE[3], OPCODE[2]);
  or or_1 (Enable, and_1_out, and_2_out);
  and and_2 (and_2_out, OPCODE[3], OPCODE[2], OPCODE[0]);
endmodule

module Flag_Decoder (
  input  [4:0] OPCODE,
  output [3:0] FLAGS
);

  wire and_1_out, and_2_out, not_1_out;

  not not_1 (not_1_out, OPCODE[4]);
  or or_1 (FLAGS[1], not_1_out, OPCODE[3]);
  and and_1 (and_1_out, OPCODE[4], OPCODE[3]);
  or or_2 (FLAGS[0], and_1_out, and_2_out);
  and and_2 (and_2_out, OPCODE[3], OPCODE[2]);

  assign FLAGS[3:2] = 2'b11;
endmodule

module Opcode_Calculator (
  input  [4:0] entry,
  output [3:0] opcode
);

  wire and_2_out, and_3_out, and_4_out, and_5_out, and_6_out, and_7_out, not_1_out, not_2_out, not_3_out,
       not_4_out;

  not not_1 (not_1_out, entry[4]);
  not not_2 (not_2_out, entry[3]);
  not not_3 (not_3_out, entry[2]);
  not not_4 (not_4_out, entry[0]);
  and and_1 (opcode[3], entry[4], not_2_out);
  and and_2 (and_2_out, not_1_out, not_2_out);
  and and_3 (and_3_out, entry[2], entry[0]);
  and and_4 (and_4_out, entry[4], entry[2]);
  and and_5 (and_5_out, not_1_out, not_2_out, entry[2]);
  and and_6 (and_6_out, not_1_out, entry[2], not_4_out);
  and and_7 (and_7_out, entry[4], not_3_out);
  or or_1 (opcode[1], and_2_out, and_3_out, and_4_out);
  or or_2 (opcode[0], and_5_out, and_6_out, and_7_out);

  assign opcode[2] = entry[3];
endmodule
